// Logisim project trab.circ as structural Verilog: 3 circuits, main circuit main
module main (
);

  wire brzr, clk, ula_mux, wbreg, wm;
  wire [1:0] dado_breg, pc_sel;
  wire [3:0] opcode, opula;
  wire [7:0] rom_1_data;
  wire [11:0] imm, jalr, multiplexer_1_out, multiplexer_2_out, multiplexer_3_out, multiplexer_4_out, pc_imm,
       PC_q, RA, ram_1_dout, RB, rd, ula_1_out_5;

  Clock clock_1 (.out(clk));
  Multiplexer #(.select(2), .width(12)) multiplexer_1 (
    .in0(rd), .in1(pc_imm), .in2(multiplexer_2_out), .in3(jalr), .out(multiplexer_1_out), .sel(pc_sel));
  Multiplexer #(.width(12)) multiplexer_2 (.in0(rd), .in1(RB), .out(multiplexer_2_out), .sel(brzr));
  Register #(.width(12)) PC (.D(multiplexer_1_out), .en(1'b1), .clk(clk), .Q(PC_q));  // open: clr
  Adder #(.width(12)) adder_1 (.a(PC_q), .b(12'h1), .out(rd));  // open: cin, cout
  ROM #(.addrWidth(12), .dataWidth(12)) rom_1 (.addr(PC_q), .data({opcode, rom_1_data}));
  Adder #(.width(12)) adder_2 (.a(PC_q), .b(imm), .out(pc_imm));  // open: cin, cout
  Adder #(.width(12)) adder_3 (.a(imm), .b(RA), .out(jalr));  // open: cin, cout
  assign imm = {{8{rom_1_data[3]}}, rom_1_data[3:0]};  // Bit_Extender bit_extender_1
  ROM #(.addrWidth(4), .dataWidth(11)) rom_2 (.addr(opcode), .data({pc_sel, wbreg, dado_breg, ula_mux, wm, opula}));
  breg breg_1 (
    .D(multiplexer_3_out), .rs1(rom_1_data[7:4]), .rs2(rom_1_data[3:0]), .w(wbreg), .rd(rom_1_data[7:4]),
    .clk(clk), .a(RA), .b(RB));
  Multiplexer #(.select(2), .width(12)) multiplexer_3 (
    .in0(ula_1_out_5), .in1(ram_1_dout), .in2(rd), .out(multiplexer_3_out), .sel(dado_breg));  // open: in3
  Multiplexer #(.width(12)) multiplexer_4 (.in0(RB), .in1(imm), .out(multiplexer_4_out), .sel(ula_mux));
  ula ula_1 (.A(RA), .B(multiplexer_4_out), .s(opula), .zero(brzr), .out_5(ula_1_out_5));
  RAM #(.addrWidth(12), .dataWidth(12), .trigger("falling")) ram_1 (
    .addr(RB), .we(wm), .oe(1'b1), .clk(clk), .din(RA), .dout(ram_1_dout));

  // Notes on the sheet:
  //   contents of rom_1 (hex, n*v repeats v):
  //   a02
  //   contents of rom_2 (hex, n*v repeats v):
  //   100 101 102 103 104 105 106 107 108 109 120 400 10 140 600 380
endmodule

module breg (
  input  [11:0] D,
  input  [3:0] rs1,
  input  [3:0] rs2,
  input  w,
  input  [3:0] rd,
  input  clk,
  output [11:0] a,
  output [11:0] b
);

  wire w0, w1, w2, w3, w4, w5, w6, w7, w8, w9, w10, w11, w12, w13, w14, w15;
  wire [11:0] multiplexer_1_out, multiplexer_2_out, multiplexer_3_out, multiplexer_4_out, multiplexer_5_out,
       multiplexer_6_out, multiplexer_7_out, multiplexer_8_out, multiplexer_9_out, multiplexer_10_out,
       multiplexer_11_out, multiplexer_12_out, multiplexer_13_out, multiplexer_14_out, multiplexer_15_out,
       multiplexer_16_out, rg0, rg1, rg2, rg3, rg4, rg5, rg6, rg7, rg8, rg9, rg10, rg11, rg12, rg13, rg14,
       rg15;

  Demultiplexer #(.select(4)) demultiplexer_1 (
    .out0(w0), .out1(w1), .out2(w2), .out3(w3), .out4(w4), .out5(w5), .out6(w6), .out7(w7), .out8(w8),
    .out9(w9), .out10(w10), .out11(w11), .out12(w12), .out13(w13), .out14(w14), .out15(w15), .in(w), .sel(rd));
  Register #(.width(12)) r0 (.D(multiplexer_1_out), .clk(clk), .Q(rg0));  // open: en, clr
  Multiplexer #(.width(12)) multiplexer_1 (.in0(rg0), .in1(D), .out(multiplexer_1_out), .sel(w0));
  Register #(.width(12)) r1 (.D(multiplexer_2_out), .clk(clk), .Q(rg1));  // open: en, clr
  Multiplexer #(.width(12)) multiplexer_2 (.in0(rg1), .in1(D), .out(multiplexer_2_out), .sel(w1));
  Register #(.width(12)) r2 (.D(multiplexer_3_out), .clk(clk), .Q(rg2));  // open: en, clr
  Multiplexer #(.width(12)) multiplexer_3 (.in0(rg2), .in1(D), .out(multiplexer_3_out), .sel(w2));
  Register #(.width(12)) r3 (.D(multiplexer_4_out), .clk(clk), .Q(rg3));  // open: en, clr
  Multiplexer #(.width(12)) multiplexer_4 (.in0(rg3), .in1(D), .out(multiplexer_4_out), .sel(w3));
  Register #(.width(12)) r4 (.D(multiplexer_5_out), .clk(clk), .Q(rg4));  // open: en, clr
  Multiplexer #(.width(12)) multiplexer_5 (.in0(rg4), .in1(D), .out(multiplexer_5_out), .sel(w4));
  Register #(.width(12)) r5 (.D(multiplexer_6_out), .clk(clk), .Q(rg5));  // open: en, clr
  Multiplexer #(.width(12)) multiplexer_6 (.in0(rg5), .in1(D), .out(multiplexer_6_out), .sel(w5));
  Register #(.width(12)) r6 (.D(multiplexer_7_out), .clk(clk), .Q(rg6));  // open: en, clr
  Multiplexer #(.width(12)) multiplexer_7 (.in0(rg6), .in1(D), .out(multiplexer_7_out), .sel(w6));
  Register #(.width(12)) r7 (.D(multiplexer_8_out), .clk(clk), .Q(rg7));  // open: en, clr
  Multiplexer #(.width(12)) multiplexer_8 (.in0(rg7), .in1(D), .out(multiplexer_8_out), .sel(w7));
  Register #(.width(12)) r8 (.D(multiplexer_9_out), .clk(clk), .Q(rg8));  // open: en, clr
  Multiplexer #(.width(12)) multiplexer_9 (.in0(rg8), .in1(D), .out(multiplexer_9_out), .sel(w8));
  Register #(.width(12)) r9 (.D(multiplexer_10_out), .clk(clk), .Q(rg9));  // open: en, clr
  Multiplexer #(.width(12)) multiplexer_10 (.in0(rg9), .in1(D), .out(multiplexer_10_out), .sel(w9));
  Register #(.width(12)) r10 (.D(multiplexer_11_out), .clk(clk), .Q(rg10));  // open: en, clr
  Multiplexer #(.width(12)) multiplexer_11 (.in0(rg10), .in1(D), .out(multiplexer_11_out), .sel(w10));
  Register #(.width(12)) r11 (.D(multiplexer_12_out), .clk(clk), .Q(rg11));  // open: en, clr
  Multiplexer #(.width(12)) multiplexer_12 (.in0(rg11), .in1(D), .out(multiplexer_12_out), .sel(w11));
  Register #(.width(12)) r12 (.D(multiplexer_13_out), .clk(clk), .Q(rg12));  // open: en, clr
  Multiplexer #(.width(12)) multiplexer_13 (.in0(rg12), .in1(D), .out(multiplexer_13_out), .sel(w12));
  Register #(.width(12)) r13 (.D(multiplexer_14_out), .clk(clk), .Q(rg13));  // open: en, clr
  Multiplexer #(.width(12)) multiplexer_14 (.in0(rg13), .in1(D), .out(multiplexer_14_out), .sel(w13));
  Register #(.width(12)) r14 (.D(multiplexer_15_out), .clk(clk), .Q(rg14));  // open: en, clr
  Multiplexer #(.width(12)) multiplexer_15 (.in0(rg14), .in1(D), .out(multiplexer_15_out), .sel(w14));
  Register #(.width(12)) r15 (.D(multiplexer_16_out), .clk(clk), .Q(rg15));  // open: en, clr
  Multiplexer #(.width(12)) multiplexer_16 (.in0(rg15), .in1(D), .out(multiplexer_16_out), .sel(w15));
  Multiplexer #(.select(4), .width(12)) multiplexer_17 (
    .in0(rg0), .in1(rg1), .in2(rg2), .in3(rg3), .in4(rg4), .in5(rg5), .in6(rg6), .in7(rg7), .in8(rg8),
    .in9(rg9), .in10(rg10), .in11(rg11), .in12(rg12), .in13(rg13), .in14(rg14), .in15(rg15), .out(a),
    .sel(rs1));
  Multiplexer #(.select(4), .width(12)) multiplexer_18 (
    .in0(rg0), .in1(rg1), .in2(rg2), .in3(rg3), .in4(rg4), .in5(rg5), .in6(rg6), .in7(rg7), .in8(rg8),
    .in9(rg9), .in10(rg10), .in11(rg11), .in12(rg12), .in13(rg13), .in14(rg14), .in15(rg15), .out(b),
    .sel(rs2));
endmodule

module ula (
  input  [11:0] A,
  input  [11:0] B,
  input  [3:0] s,
  output zero,
  output [11:0] out_5
);

  wire [11:0] adder_1_out, and_1_out, divider_1_out, multiplier_1_out, not_1_out, or_1_out, shifter_1_out,
       shifter_2_out, subtractor_1_out, undriven, undriven_2, undriven_3, undriven_4, undriven_5, undriven_6,
       xor_1_out;

  Adder #(.width(12)) adder_1 (.a(A), .b(B), .out(adder_1_out));  // open: cin, cout
  Subtractor #(.width(12)) subtractor_1 (.a(A), .b(B), .out(subtractor_1_out));  // open: bin, bout
  Multiplier #(.width(12)) multiplier_1 (.a(A), .b(B), .out(multiplier_1_out));  // open: cin, cout
  Divider #(.width(12)) divider_1 (.a(A), .b(B), .out(divider_1_out));  // open: upper, rem
  assign and_1_out = A & B;  // AND_Gate and_1, 12 bits wide
  assign or_1_out = A | B;  // OR_Gate or_1, 12 bits wide
  assign not_1_out = ~B;  // NOT_Gate not_1, 12 bits wide
  assign xor_1_out = A ^ B;  // XOR_Gate xor_1, 12 bits wide
  Shifter #(.shift("lr"), .width(12)) shifter_1 (.in(A), .\dist (B[3:0]), .out(shifter_1_out));
  Shifter #(.width(12)) shifter_2 (.in(A), .\dist (B[3:0]), .out(shifter_2_out));
  Multiplexer #(.select(4), .width(12)) multiplexer_1 (
    .in0(adder_1_out), .in1(subtractor_1_out), .in2(multiplier_1_out), .in3(divider_1_out), .in4(and_1_out),
    .in5(or_1_out), .in6(not_1_out), .in7(xor_1_out), .in8(shifter_1_out), .in9(shifter_2_out),
    .in10(undriven), .in11(undriven_2), .in12(undriven_3), .in13(undriven_4), .in14(undriven_5),
    .in15(undriven_6), .out(out_5), .sel(s));
  Comparator #(.width(12)) comparator_1 (.a({12{1'b0}}), .b(A), .eq(zero));  // open: gt, lt
endmodule
